// Logisim project Logique.circ as structural Verilog: 1 circuit, main circuit ACAR
module ACAR (
  input  B,
  input  C,
  input  A,
  input  D,
  output Moteur_droite,
  output Moteur_gauche
);

  not not_1 (Moteur_droite, B);
  not not_2 (Moteur_gauche, C);

  // Notes on the sheet:
  //   0 = Arrière
  //   1 = Avant
  //   Sens des moteurs :
endmodule
